# Fritzing sketch 洗衣机 (saved by Fritzing 0.7.12b)
breadboards: 1

parts:
  S1 = Pushbutton [package="[THT]"]
  S2 = Pushbutton [package="[THT]"]
  Arduino1 = Arduino
  S3 = Pushbutton [package="[THT]"]
  S4 = Pushbutton [package="[THT]"]

nets:
  N1: S1.Pin_1, S1.Pin_2, S2.Pin_1, S2.Pin_2, S3.Pin_1, S3.Pin_2, S4.Pin_1, S4.Pin_2
  N2: S1.Pin_3, S1.Pin_4, S2.Pin_3, S2.Pin_4, Arduino1.D7, Arduino1.D6, Arduino1.D5, Arduino1.D1TX, S3.Pin_3, S3.Pin_4, S4.Pin_3, S4.Pin_4

notes:
  开始/暂停
  程序
  水位
